// Logisim project My Smart Water Tank.circ as structural Verilog
module Smart_Water_Tank (
  input  S0,
  input  S1,
  input  S2,
  input  S3,
  input  RESET,
  output L1,
  output FULL,
  output PUMP,
  output L0,
  output R1,
  output R0,
  output ALARM,
  output out_13,
  output out_14
);

  wire and_2_out, and_3_out, and_5_out, and_6_out, and_7_out, clock_1_out, EN_out, not_1_out, not_2_out,
       not_4_out, not_5_out, not_6_out, or_3_out, or_4_out, or_5_out, or_6_out;

  Clock clock_1 (.out(clock_1_out));
  or or_1 (L1, S2, S3);
  or or_2 (L0, S1, S3);
  not not_1 (not_1_out, RESET);
  not not_2 (not_2_out, RESET);
  and EN (EN_out, not_2_out, FULL);
  and and_1 (FULL, L1, L0);
  and and_2 (and_2_out, L1, not_1_out);
  and and_3 (and_3_out, L0, not_1_out);
  D_Flip_Flop FF1 (.D(and_2_out), .clk(clock_1_out), .Q(R1));  // open: Qn, preset, reset
  D_Flip_Flop FF0 (.D(and_3_out), .clk(clock_1_out), .Q(R0));  // open: Qn, preset, reset
  D_Flip_Flop Q1 (.D(and_6_out), .clk(clock_1_out), .Q(out_13));  // open: Qn, preset, reset
  D_Flip_Flop Q0 (.D(and_5_out), .clk(clock_1_out), .Q(out_14));  // open: Qn, preset, reset
  LED led_1 (.in(PUMP));
  not not_3 (PUMP, FULL);
  not not_4 (not_4_out, R1);
  not not_5 (not_5_out, R0);
  not not_6 (not_6_out, out_14);
  and and_4 (ALARM, out_13, out_14);
  or or_3 (or_3_out, out_13, not_6_out);
  or or_4 (or_4_out, out_13, out_14);
  LED led_2 (.in(ALARM));
  and and_5 (and_5_out, or_3_out, EN_out);
  and and_6 (and_6_out, or_4_out, EN_out);
  or or_5 (or_5_out, R1, not_5_out);
  and and_7 (and_7_out, not_4_out, not_5_out);
  or or_6 (or_6_out, not_4_out, R0);
  _7_Segment_Display u_7_segment_display_1 (
    .g(R1), .f(and_7_out), .a(or_5_out), .b(1'b1), .e(not_5_out), .d(or_5_out), .c(or_6_out));  // open: dp
endmodule
